// Logisim project sap1_v8c.circ as structural Verilog: 7 circuits, main circuit main
module main (
  input  Reset,
  output [3:0] Comando,
  output [7:0] Valor,
  output [7:0] out_4,
  output [3:0] out_5,
  output [7:0] out_6,
  output [3:0] out_7,
  output [3:0] out_8,
  output [7:0] out_9,
  output [7:0] out_10,
  output [7:0] out_11,
  output [7:0] RI_data_IN,
  output [3:0] ADR_Val,
  output [3:0] ADR_Com,
  output out_15,
  output out_16,
  output out_17,
  output out_18,
  output out_19,
  output out_20,
  output out_21,
  output out_22,
  output out_23,
  output out_24,
  output out_25,
  output out_26,
  output T1,
  output T2,
  output T3,
  output T4,
  output T5,
  output T6
);

  wire and_1_out, and_2_out, CLK, d_ff_5_qn, nCLK, nor_1_out, not_1_out, or_1_out;
  wire [3:0] counter_1_q, CS_mod_data, REM_mod_addr_out;
  wire [7:0] acumulador_1_a_dataout1, register_1_q, registrador_b_6a147718_1_b_dataout, rom_1_data;

  ROM #(.addrWidth(4)) rom_1 (.addr(REM_mod_addr_out), .data(rom_1_data));
  ROM #(.addrWidth(4), .dataWidth(4)) CS_mod (.addr(ADR_Com), .data(CS_mod_data));
  CP CP_mod (.Cpp(out_24), .nCLK(nCLK), .CLR(Reset), .Ep(out_26), .output2(out_7), .CP_dataOut(ADR_Val));
  REM REM_mod (.CLK(CLK), .nLM(out_25), .ADDR_In(ADR_Val), .ADDR_Out(REM_mod_addr_out));
  REGISTRADOR_DE_INSTRUCOES_2d63c7b0 RI (
    .nLi(out_16), .CLK(CLK), .CLR(Reset), .RI2_dataIn(out_4), .nEi(out_21), .RI2_dataOut1(ADR_Com),
    .RI2_dataOut2(ADR_Val));
  nor nor_1 (nor_1_out, T1, T2, T3, T4, T5, T6);
  and and_1 (and_1_out, CLK, out_23);
  D_Flip_Flop #(.trigger("falling")) D1 (
    .clk(CLK), .D(nor_1_out), .Q(T1), .preset(nor_1_out), .reset(Reset));  // open: Qn
  assign out_4 = and_1_out ? rom_1_data : 8'bz;  // Controlled_Buffer controlled_buffer_1
  D_Flip_Flop #(.trigger("falling")) d_ff_1 (.clk(CLK), .D(T1), .Q(T2), .reset(Reset));  // open: Qn, preset
  ROM #(.addrWidth(4), .dataWidth(12)) rom_2 (
    .addr(counter_1_q),
    .data({out_26, out_25, out_24, out_23, out_22, out_21, out_20, out_19, out_18, out_17, out_16, out_15}));
  Counter #(.max('hf), .width(4)) counter_1 (
    .load(T3), .D(CS_mod_data), .Q(counter_1_q), .clk(nCLK), .clr(or_1_out));  // open: count, carry, up
  or or_1 (or_1_out, and_2_out, Reset);
  and and_2 (and_2_out, d_ff_5_qn, not_1_out);
  not not_1 (not_1_out, d_ff_5_qn);
  D_Flip_Flop #(.trigger("falling")) d_ff_2 (.clk(CLK), .D(T2), .Q(T3), .reset(Reset));  // open: Qn, preset
  Clock clock_1 (.out(CLK));
  D_Flip_Flop #(.trigger("falling")) d_ff_3 (.clk(CLK), .D(T3), .Q(T4), .reset(Reset));  // open: Qn, preset
  Register #(.trigger("falling")) register_1 (.D(out_4), .en(out_20), .Q(register_1_q), .clk(CLK), .clr(Reset));
  not not_2 (nCLK, CLK);
  D_Flip_Flop #(.trigger("falling")) d_ff_4 (.clk(CLK), .D(T4), .Q(T5), .reset(Reset));  // open: Qn, preset
  Acumulador acumulador_1 (
    .nLa(out_22), .CLK(CLK), .Ea(out_15), .A_dataIn(out_4), .A_dataOut2(out_4),
    .A_dataOut1(acumulador_1_a_dataout1));
  Somador_Subtrator somador_subtrator_1 (
    .B_data(registrador_b_6a147718_1_b_dataout), .A_data(acumulador_1_a_dataout1), .Eu(out_18), .Su(out_17),
    .A_dataOut2(out_4));
  Registrador_B_6a147718 registrador_b_6a147718_1 (
    .nLb(out_19), .B_dataIn(out_4), .B_dataOut(registrador_b_6a147718_1_b_dataout));
  Hex_Digit_Display hex_digit_display_1 (.value(register_1_q[7:4]));  // open: dp
  Hex_Digit_Display hex_digit_display_2 (.value(register_1_q[3:0]));  // open: dp
  D_Flip_Flop #(.trigger("falling")) d_ff_5 (.clk(CLK), .D(T5), .Q(T6), .Qn(d_ff_5_qn), .reset(Reset));  // open: preset

  assign Comando = ADR_Val;
  assign out_5 = ADR_Val;
  assign out_6 = out_4;
  assign out_8 = ADR_Val;
  assign out_9 = out_4;
  assign out_10 = out_4;
  assign out_11 = out_4;
  assign RI_data_IN = out_4;
  assign Valor = out_4;

  // Other names for the same wires on the sheet: Ea = out_15; nLi = out_16; Su = out_17; Eu = out_18; nLb = out_19;
  //   nLo = out_20; nEi = out_21; nLa = out_22; nCE = out_23; Cpp = out_24; nLM = out_25; Ep = out_26; CLR = Reset;
  //   T3_D = T3

  // Notes on the sheet:
  //   contents of rom_1 (hex, n*v repeats v):
  //   1f 2e 2d 3c e0 f0 6*0 1 4 3 2
  //   contents of CS_mod (hex, n*v repeats v):
  //   0 3 6 9 10*0 c
  //   contents of rom_2 (hex, n*v repeats v):
  //   c00 102 200 440 180 0 440 110 88 440 110 8c 21
endmodule

module CP (
  input  Cpp,
  input  nCLK,
  input  CLR,
  input  Ep,
  output [3:0] CP_dataOut,
  output [3:0] output2
);

  Counter #(.max('hf), .width(4)) counter_1 (
    .count(Cpp), .Q(output2), .clk(nCLK), .clr(CLR));  // open: load, D, carry, up
  assign CP_dataOut = Ep ? output2 : 4'bz;  // Controlled_Buffer controlled_buffer_1
endmodule

module Acumulador (
  input  [7:0] A_dataIn,
  input  nLa,
  input  CLK,
  input  Ea,
  output [7:0] A_dataOut1,
  output [7:0] A_dataOut2
);

  Register #(.trigger("falling")) register_1 (.D(A_dataIn), .en(nLa), .Q(A_dataOut1), .clk(CLK));  // open: clr
  assign A_dataOut2 = Ea ? A_dataOut1 : 8'bz;  // Controlled_Buffer controlled_buffer_1
endmodule

module Somador_Subtrator (
  input  Su,
  input  [7:0] B_data,
  input  [7:0] A_data,
  input  Eu,
  output [7:0] A_dataOut2
);

  wire [7:0] adder_1_out, xor_1_out;

  assign xor_1_out = {8{Su}} ^ B_data;  // XOR_Gate xor_1, 8 bits wide
  Adder adder_1 (.a(xor_1_out), .b(A_data), .out(adder_1_out), .cin(Su));  // open: cout
  assign A_dataOut2 = Eu ? adder_1_out : 8'bz;  // Controlled_Buffer controlled_buffer_1
endmodule

module Registrador_B_6a147718 (
  input  [7:0] B_dataIn,
  input  nLb,
  output [7:0] B_dataOut
);

  wire clock_1_out;

  Clock clock_1 (.out(clock_1_out));
  Register #(.trigger("high")) register_1 (.D(B_dataIn), .en(nLb), .Q(B_dataOut), .clk(clock_1_out));  // open: clr
endmodule

module REM (
  input  [3:0] ADDR_In,
  input  nLM,
  input  CLK,
  output [3:0] ADDR_Out
);

  Register #(.width(4)) register_1 (.D(ADDR_In), .en(nLM), .Q(ADDR_Out), .clk(CLK));  // open: clr
endmodule

// RI
module REGISTRADOR_DE_INSTRUCOES_2d63c7b0 (
  input  [7:0] RI2_dataIn,
  input  nLi,
  input  CLK,
  input  CLR,
  input  nEi,
  output [3:0] RI2_dataOut2,
  output [3:0] RI2_dataOut1
);

  wire [3:0] register_1_q;

  Register #(.trigger("falling")) register_1 (
    .D(RI2_dataIn), .en(nLi), .Q({RI2_dataOut1, register_1_q}), .clk(CLK), .clr(CLR));
  assign RI2_dataOut2 = nEi ? register_1_q : 4'bz;  // Controlled_Buffer controlled_buffer_1
endmodule
